// Logisim project computador-8bits.circ as structural Verilog: 1 circuit, main circuit main
module main (
  input  A,
  input  C,
  input  B,
  input  A8,
  input  A7,
  input  A6,
  input  A5,
  input  A4,
  input  A3,
  input  A2,
  input  A1,
  input  S_N,
  input  B8,
  input  B7,
  input  B6,
  input  B5,
  input  B4,
  input  B3,
  input  B2,
  input  B1,
  output out_21,
  output Cout,
  output S8,
  output S7,
  output S6,
  output S5,
  output S4,
  output S3,
  output S2,
  output S1
);

  wire and_1_out, and_2_out, and_3_out, and_4_out, and_5_out, and_6_out, and_7_out, and_8_out, and_9_out,
       and_10_out, and_11_out, and_12_out, and_13_out, and_14_out, and_15_out, and_16_out, and_17_out,
       and_18_out, not_1_out, or_1_out, or_2_out, or_3_out, or_4_out, or_5_out, or_6_out, or_7_out,
       xor_1_out, xor_2_out, xor_3_out, xor_4_out, xor_5_out, xor_6_out, xor_7_out, xor_8_out, xor_9_out,
       xor_10_out, xor_13_out, xor_14_out, xor_17_out, xor_18_out, xor_19_out, xor_20_out;

  xor xor_1 (xor_1_out, B8, S_N);
  xor xor_2 (xor_2_out, B7, S_N);
  xor xor_3 (xor_3_out, B6, S_N);
  xor xor_4 (xor_4_out, B5, S_N);
  xor xor_5 (xor_5_out, B4, S_N);
  xor xor_6 (xor_6_out, B3, S_N);
  xor xor_7 (xor_7_out, B1, S_N);
  xor xor_8 (xor_8_out, B2, S_N);
  xor xor_9 (xor_9_out, A1, xor_7_out);
  xor xor_10 (xor_10_out, A3, xor_6_out);
  xor xor_11 (S1, xor_9_out, S_N);
  and and_1 (and_1_out, A1, xor_7_out);
  and and_2 (and_2_out, xor_9_out, S_N);
  xor xor_12 (S3, xor_10_out, or_5_out);
  and and_3 (and_3_out, A3, xor_6_out);
  and and_4 (and_4_out, xor_10_out, or_5_out);
  xor xor_13 (xor_13_out, A5, xor_4_out);
  xor xor_14 (xor_14_out, A7, xor_2_out);
  or or_1 (or_1_out, and_1_out, and_2_out);
  or or_2 (or_2_out, and_3_out, and_4_out);
  xor xor_15 (S5, xor_13_out, or_6_out);
  and and_5 (and_5_out, A5, xor_4_out);
  or or_3 (or_3_out, and_5_out, and_6_out);
  and and_6 (and_6_out, xor_13_out, or_6_out);
  xor xor_16 (S7, xor_14_out, or_7_out);
  and and_7 (and_7_out, A7, xor_2_out);
  and and_8 (and_8_out, xor_14_out, or_7_out);
  or or_4 (or_4_out, and_7_out, and_8_out);
  xor xor_17 (xor_17_out, A2, xor_8_out);
  xor xor_18 (xor_18_out, A4, xor_5_out);
  xor xor_19 (xor_19_out, A6, xor_3_out);
  xor xor_20 (xor_20_out, A8, xor_1_out);
  xor xor_21 (S2, xor_17_out, or_1_out);
  and and_9 (and_9_out, A2, xor_8_out);
  and and_10 (and_10_out, xor_17_out, or_1_out);
  xor xor_22 (S4, xor_18_out, or_2_out);
  and and_11 (and_11_out, A4, xor_5_out);
  and and_12 (and_12_out, xor_18_out, or_2_out);
  xor xor_23 (S6, xor_19_out, or_3_out);
  and and_13 (and_13_out, A6, xor_3_out);
  and and_14 (and_14_out, xor_19_out, or_3_out);
  and and_15 (and_15_out, A8, xor_1_out);
  and and_16 (and_16_out, xor_20_out, or_4_out);
  or or_5 (or_5_out, and_9_out, and_10_out);
  or or_6 (or_6_out, and_11_out, and_12_out);
  or or_7 (or_7_out, and_13_out, and_14_out);
  xor xor_24 (S8, xor_20_out, or_4_out);
  or or_8 (Cout, and_15_out, and_16_out);
  not not_1 (not_1_out, C);
  and and_17 (and_17_out, C, B);
  and and_18 (and_18_out, A, not_1_out);
  or or_9 (out_21, and_18_out, and_17_out);
endmodule
